# Fritzing sketch 2n2222 Project (saved by Fritzing 0.9.3b)
breadboards: 1

parts:
  Q1 = NPN-Transistor [package="TO92 [THT]"]
  R1 = Resistor [tolerance=±5% resistance=1k package=THT]
  J1 = Screw terminal - 2 pins [package=THT]
  J2 = Screw terminal - 2 pins [package=THT]
  BAT1 = BC9VPC [package=bc9vpc]
  MCU1 = Raspberry Pi Zero
  F1 = Fan - Ventilador [package=THT]
  M1 = fc-51 [package=THT]

nets:
  N1: Q1.E, MCU1.pin_6, MCU1.pin_9, MCU1.pin_30, MCU1.pin_39, M1.pin2
  N2: Q1.C, R1.Pin_0
  N3: R1.Pin_1, MCU1.pin_11
  N4: J1.pin1, BAT1.V-
  N5: J2.pin1, F1.GND
  N6: BAT1.V+, F1.5V
  N7: MCU1.pin_2, MCU1.pin_4, M1.pin3
  N8: MCU1.pin_13, M1.pin1

custom parts:
  Fan - Ventilador: Ventilador de 2 pines, se encuentra comunmente en computadoras de escritorio
