# Fritzing sketch Relay Project (saved by Fritzing 0.9.3b)

parts:
  BAT1 = BC9VPC [package=bc9vpc]
  MCU1 = Raspberry Pi Zero
  F1 = Fan - Ventilador [package=THT]
  M1 = fc-51 [package=THT]
  U1 = 4-Channel 5v Relay Shield [package=relay-4ch5v10a]

nets:
  N1: BAT1.V+, F1.5V
  N2: BAT1.V-, U1.K1-On
  N3: MCU1.pin_2, MCU1.pin_4, M1.pin3, U1.VCC
  N4: MCU1.pin_6, MCU1.pin_39, M1.pin2, U1.GND
  N5: MCU1.pin_11, U1.IN1
  N6: MCU1.pin_13, M1.pin1
  N7: F1.GND, U1.K1-Off

custom parts:
  Fan - Ventilador: Ventilador de 2 pines, se encuentra comunmente en computadoras de escritorio
  4-Channel 5v Relay Shield: 4 Channel 5v Relay Shield w. 2x SPD-06VDC-SD-C
